// Logisim project test.circ as structural Verilog
module main (
  input  in_1,
  input  in_2
);

  wire not_1_out, not_2_out, not_3_out, or_1_out, test_1_out_2, test_1_out_3;

  or or_1 (or_1_out, in_1, in_2);
  not not_1 (not_1_out, or_1_out);
  not not_2 (not_2_out, test_1_out_2);
  test test_1 (.c(not_1_out), .out_2(test_1_out_2), .out_3(test_1_out_3));
  not not_3 (not_3_out, test_1_out_3);
  // AND_Gate and_1 has open pins: in0=not_2_out, in1=not_3_out, out=open
endmodule

module test (
  input  c,
  output out_2,
  output out_3
);


  assign out_2 = c;
  assign out_3 = c;
endmodule
